// Logisim project main.circ as structural Verilog: 3 circuits, main circuit main
module main (
  input  Reset
);

  wire [4:0] instr_counter_1_addressout;

  instr_counter instr_counter_1 (
    .reset(Reset), .AddressOut(instr_counter_1_addressout));  // open: LoadAddress, AddressIn
  ROM #(.addrWidth(5)) rom_1 (.addr(instr_counter_1_addressout));  // open: data, sel
endmodule

// RAM
module RAM_module (
  input  [7:0] DataIn,
  input  [7:0] Address,
  input  Reset,
  input  MemWrite,
  output [7:0] DataOut
);

  wire clock_1_out, not_1_out;

  Clock clock_1 (.out(clock_1_out));
  not not_1 (not_1_out, MemWrite);
  assign DataOut = MemWrite ? DataIn : 8'bz;  // Controlled_Buffer controlled_buffer_1
  RAM ram_1 (.addr(Address), .data(DataOut), .sel(1'b1), .clk(clock_1_out), .ld(not_1_out), .clr(Reset));
endmodule

// IC
module instr_counter (
  input  LoadAddress,
  input  [4:0] AddressIn,
  input  reset,
  output [4:0] AddressOut
);

  wire clock_1_out, not_1_out;

  not not_1 (not_1_out, LoadAddress);
  Counter #(.width(5), .max('h1f), .ongoal("stay")) counter_1 (
    .load(LoadAddress), .D(AddressIn), .count(not_1_out), .Q(AddressOut), .clk(clock_1_out), .clr(reset));  // open: carry
  Clock clock_1 (.out(clock_1_out));
endmodule
